# Fritzing sketch red-phone (saved by Fritzing 0.9.3b)
circuit board: 8.46667cm x 5.64444cm
breadboards: 1

parts:
  Raspberry_Pi_Zero1 = Raspberry Pi Zero
  Q1 = NPN-Transistor [package="TO92 [THT]"]
  Q2 = NPN-Transistor [package="TO92 [THT]"]
  SP1 = SPEAKER [package=pcb_mount_speaker]
  L1 = Solenoid
  L2 = Solenoid

nets:
  N1: Raspberry_Pi_Zero1.GND, Q1.E, Q2.E, SP1.+
  N2: Raspberry_Pi_Zero1.GPIO17, Q1.B
  N3: Raspberry_Pi_Zero1.GPIO27, Q2.B
  N4: Raspberry_Pi_Zero1.GPIO13, SP1.-
  N5: Raspberry_Pi_Zero1.5V, L1.pin2, L2.pin2
  N6: Q1.C, L1.pin1
  N7: Q2.C, L2.pin1
